// Logisim project RegisterFile.circ as structural Verilog: 1 circuit, main circuit RegisterFile
module RegisterFile (
  input  [3:0] readRegister1,
  input  [3:0] writeReg,
  input  [3:0] readRegister2,
  input  [15:0] write_data,
  input  regwrite,
  input  in_6,
  output [15:0] readData1,
  output [15:0] readData2
);

  wire and_1_out, and_2_out, and_3_out, and_4_out, and_5_out, and_6_out, and_7_out, and_8_out, and_9_out,
       and_10_out, and_11_out, and_12_out, and_13_out, and_14_out, and_15_out, and_16_out, decoder_1_out0,
       decoder_1_out1, decoder_1_out2, decoder_1_out3, decoder_1_out4, decoder_1_out5, decoder_1_out6,
       decoder_1_out7, decoder_1_out8, decoder_1_out9, decoder_1_out10, decoder_1_out11, decoder_1_out12,
       decoder_1_out13, decoder_1_out14, decoder_1_out15;
  wire [15:0] Reg1_q, Reg2_q, Reg3_q, Reg4_q, Reg5_q, Reg6_q, Reg7_q, Reg8_q, Reg9_q, Reg10_q, Reg11_q,
       Reg12_q, Reg13_q, Reg14_q, Reg15_q, Reg16_q;

  Decoder #(.select(4)) decoder_1 (
    .out0(decoder_1_out0), .out1(decoder_1_out1), .out2(decoder_1_out2), .out3(decoder_1_out3),
    .out4(decoder_1_out4), .out5(decoder_1_out5), .out6(decoder_1_out6), .out7(decoder_1_out7),
    .out8(decoder_1_out8), .out9(decoder_1_out9), .out10(decoder_1_out10), .out11(decoder_1_out11),
    .out12(decoder_1_out12), .out13(decoder_1_out13), .out14(decoder_1_out14), .out15(decoder_1_out15),
    .sel(writeReg));  // open: en
  and and_1 (and_1_out, decoder_1_out0, regwrite);
  and and_2 (and_2_out, decoder_1_out1, regwrite);
  and and_3 (and_3_out, decoder_1_out2, regwrite);
  and and_4 (and_4_out, decoder_1_out3, regwrite);
  and and_5 (and_5_out, decoder_1_out4, regwrite);
  and and_6 (and_6_out, decoder_1_out5, regwrite);
  and and_7 (and_7_out, decoder_1_out6, regwrite);
  and and_8 (and_8_out, decoder_1_out7, regwrite);
  and and_9 (and_9_out, decoder_1_out8, regwrite);
  and and_10 (and_10_out, decoder_1_out9, regwrite);
  and and_11 (and_11_out, decoder_1_out10, regwrite);
  and and_12 (and_12_out, decoder_1_out11, regwrite);
  and and_13 (and_13_out, decoder_1_out12, regwrite);
  and and_14 (and_14_out, decoder_1_out13, regwrite);
  and and_15 (and_15_out, decoder_1_out14, regwrite);
  and and_16 (and_16_out, decoder_1_out15, regwrite);
  Register #(.width(16)) Reg1 (.D(write_data), .en(and_1_out), .Q(Reg1_q), .clk(in_6), .clr(1'b0));
  Register #(.width(16)) Reg2 (.D(write_data), .en(and_2_out), .Q(Reg2_q), .clk(in_6), .clr(1'b0));
  Register #(.width(16)) Reg3 (.D(write_data), .en(and_3_out), .Q(Reg3_q), .clk(in_6), .clr(1'b0));
  Register #(.width(16)) Reg4 (.D(write_data), .en(and_4_out), .Q(Reg4_q), .clk(in_6), .clr(1'b0));
  Register #(.width(16)) Reg5 (.D(write_data), .en(and_5_out), .Q(Reg5_q), .clk(in_6), .clr(1'b0));
  Register #(.width(16)) Reg6 (.D(write_data), .en(and_6_out), .Q(Reg6_q), .clk(in_6), .clr(1'b0));
  Register #(.width(16)) Reg7 (.D(write_data), .en(and_7_out), .Q(Reg7_q), .clk(in_6), .clr(1'b0));
  Register #(.width(16)) Reg8 (.D(write_data), .en(and_8_out), .Q(Reg8_q), .clk(in_6), .clr(1'b0));
  Register #(.width(16)) Reg9 (.D(write_data), .en(and_9_out), .Q(Reg9_q), .clk(in_6), .clr(1'b0));
  Register #(.width(16)) Reg10 (.D(write_data), .en(and_10_out), .Q(Reg10_q), .clk(in_6), .clr(1'b0));
  Register #(.width(16)) Reg11 (.D(write_data), .en(and_11_out), .Q(Reg11_q), .clk(in_6), .clr(1'b0));
  Register #(.width(16)) Reg12 (.D(write_data), .en(and_12_out), .Q(Reg12_q), .clk(in_6), .clr(1'b0));
  Register #(.width(16)) Reg13 (.D(write_data), .en(and_13_out), .Q(Reg13_q), .clk(in_6), .clr(1'b0));
  Register #(.width(16)) Reg14 (.D(write_data), .en(and_14_out), .Q(Reg14_q), .clk(in_6), .clr(1'b0));
  Register #(.width(16)) Reg15 (.D(write_data), .en(and_15_out), .Q(Reg15_q), .clk(in_6), .clr(1'b0));
  Register #(.width(16)) Reg16 (.D(write_data), .en(and_16_out), .Q(Reg16_q), .clk(in_6), .clr(1'b0));
  Multiplexer #(.select(4), .width(16)) multiplexer_1 (
    .in0(Reg1_q), .in1(Reg2_q), .in2(Reg3_q), .in3(Reg4_q), .in4(Reg5_q), .in5(Reg6_q), .in6(Reg7_q),
    .in7(Reg8_q), .in8(Reg9_q), .in9(Reg10_q), .in10(Reg11_q), .in11(Reg12_q), .in12(Reg13_q),
    .in13(Reg14_q), .in14(Reg15_q), .in15(Reg16_q), .out(readData1), .sel(readRegister1));  // open: en
  Multiplexer #(.select(4), .width(16)) multiplexer_2 (
    .in0(Reg1_q), .in1(Reg2_q), .in2(Reg3_q), .in3(Reg4_q), .in4(Reg5_q), .in5(Reg6_q), .in6(Reg7_q),
    .in7(Reg8_q), .in8(Reg9_q), .in9(Reg10_q), .in10(Reg11_q), .in11(Reg12_q), .in12(Reg13_q),
    .in13(Reg14_q), .in14(Reg15_q), .in15(Reg16_q), .out(readData2), .sel(readRegister2));  // open: en
endmodule
