// Logisim project alu control.circ as structural Verilog: 1 circuit, main circuit ALU control
module ALU_control (
  input  [3:0] \function ,
  input  [2:0] ALUOp,
  output [2:0] opselector
);

  wire [2:0] multiplexer_2_out, multiplexer_3_out;

  Multiplexer #(.width(3)) multiplexer_1 (
    .in0(multiplexer_3_out), .in1(\function [2:0]), .out(opselector), .sel(ALUOp[2]));  // open: en
  Multiplexer #(.width(3)) multiplexer_2 (
    .in0(3'b000), .in1(3'b100), .out(multiplexer_2_out), .sel(ALUOp[0]));  // open: en
  Multiplexer #(.width(3)) multiplexer_3 (
    .in0(multiplexer_2_out), .in1(3'b101), .out(multiplexer_3_out), .sel(ALUOp[1]));  // open: en
endmodule
