// Logisim project controlunit.circ as structural Verilog: 1 circuit, main circuit control unit
module control_unit (
  input  [3:0] opcode,
  output RegDst,
  output Jump,
  output Branch,
  output BNE,
  output MemRead,
  output MemtoReg,
  output MemWrite,
  output ALUSrc,
  output RegWrite,
  output [2:0] ALUOp
);

  and R_type (ALUOp[2], ~opcode[3], ~opcode[2], ~opcode[1], ~opcode[0]);  // AND_Gate
  and lw (ALUOp[0], ~opcode[3], ~opcode[2], ~opcode[1], opcode[0]);  // AND_Gate
  and sw (ALUOp[0], ~opcode[3], ~opcode[2], opcode[1], ~opcode[0]);  // AND_Gate
  and beq (ALUOp[1], ~opcode[3], ~opcode[2], opcode[1], opcode[0]);  // AND_Gate
  and u_bne (ALUOp[1], ~opcode[3], opcode[2], ~opcode[1], ~opcode[0]);  // AND_Gate
  and u_jump (Jump, ~opcode[3], opcode[2], opcode[1], opcode[0]);  // AND_Gate
  or or_1 (ALUSrc, ALUOp[0], ALUOp[0]);
  or or_2 (RegWrite, ALUOp[0], ALUOp[2]);

  assign BNE = ALUOp[1];
  assign Branch = ALUOp[1];
  assign MemRead = ALUOp[0];
  assign MemtoReg = ALUOp[0];
  assign MemWrite = ALUOp[0];
  assign RegDst = ALUOp[2];
endmodule
