// Logisim project main.circ as structural Verilog: 1 circuit, main circuit main
module main (
  input  in_1,
  output [19:0] out_2
);

  wire and_1_out, and_2_out, clock_1_out, control_unit_1_p2, control_unit_1_p3, control_unit_1_p4,
       control_unit_1_p5, control_unit_1_p6, control_unit_1_p7, control_unit_1_p8, control_unit_1_p9,
       control_unit_1_p10, or_1_out, or_2_out, registerfile_1_p7, undriven;
  wire [2:0] alu_control_1_opselector, control_unit_1_p11;
  wire [3:0] multiplexer_1_out;
  wire [15:0] alu_1_p1, bit_extender_2_out, multiplexer_3_out, ram_1_data, registerfile_1_p4,
       registerfile_1_p8;
  wire [19:0] adder_1_out, adder_2_out, bit_extender_1_out, pc_q, rom_1_data;

  Register #(.width(20)) pc (.D(out_2), .Q(pc_q), .clk(clock_1_out), .clr(in_1));  // open: en
  Clock clock_1 (.out(clock_1_out));
  Adder #(.width(20)) adder_1 (.a(20'h4), .b(pc_q), .out(adder_1_out));  // open: cin, cout
  ROM #(.addrWidth(20), .dataWidth(20)) rom_1 (.addr(pc_q), .data(rom_1_data));  // open: sel
  assign bit_extender_1_out = {{4{1'b0}}, bit_extender_2_out};  // Bit_Extender bit_extender_1
  // control_unit control_unit_1: pin names not known; wires that end beside it: rom_1_data[19:16], control_unit_1_p2, control_unit_1_p3, control_unit_1_p4, control_unit_1_p5, control_unit_1_p6, control_unit_1_p7, control_unit_1_p8, control_unit_1_p9, control_unit_1_p10, control_unit_1_p11
  assign bit_extender_2_out = {{8{rom_1_data[3]}}, {rom_1_data[3:0], rom_1_data[7:4]}};  // Bit_Extender bit_extender_2
  Adder #(.width(20)) adder_2 (.a(adder_1_out), .b(bit_extender_1_out), .out(adder_2_out));  // open: cin, cout
  Multiplexer #(.width(4), .enable("false")) multiplexer_1 (
    .in0(rom_1_data[11:8]), .in1(rom_1_data[7:4]), .out(multiplexer_1_out), .sel(control_unit_1_p2));
  Multiplexer #(.width(20), .enable("false")) multiplexer_2 (
    .in0(adder_1_out), .in1(adder_2_out), .out(out_2), .sel(or_1_out));
  // RegisterFile registerfile_1: pin names not known; wires that end beside it: rom_1_data[15:12], rom_1_data[11:8], multiplexer_1_out, registerfile_1_p4, control_unit_1_p10, clock_1_out, registerfile_1_p7, registerfile_1_p8
  ALU_control alu_control_1 (
    .\function (rom_1_data[3:0]), .ALUOp(control_unit_1_p11), .opselector(alu_control_1_opselector));
  Multiplexer #(.width(16), .enable("false")) multiplexer_3 (
    .in0(registerfile_1_p8), .in1(bit_extender_2_out), .out(multiplexer_3_out), .sel(control_unit_1_p9));
  or or_1 (or_1_out, or_2_out, control_unit_1_p3);
  and and_1 (and_1_out, control_unit_1_p4, undriven);
  or or_2 (or_2_out, and_1_out, and_2_out);
  and and_2 (and_2_out, control_unit_1_p5, ~undriven);  // AND_Gate
  // alu alu_1: pin names not known; wires that end beside it: alu_1_p1
  RAM #(.addrWidth(16), .dataWidth(16), .bus("separate")) ram_1 (
    .addr(alu_1_p1), .din(registerfile_1_p8), .data(ram_1_data), .str(control_unit_1_p8), .clk(clock_1_out),
    .ld(control_unit_1_p6));  // open: sel, clr
  Multiplexer #(.width(16), .enable("false")) multiplexer_4 (
    .in1(alu_1_p1), .out(registerfile_1_p4), .sel(control_unit_1_p7));  // open: in0

  // Notes on the sheet:
  //   contents of rom_1 (hex, n*v repeats v):
  //   101 11100 11010 11010 1011 1010 65789*0 1110 4105*0 1110 11111 111 1 1
endmodule
